# Fritzing sketch blinkyBusCube (saved by Fritzing 0.9.10b)
breadboards: 1

parts:
  LED1 = LED - 5mm [color="Red (633nm)" current=0.030 package="5 mm [THT]"]
  LED2 = LED - 5mm [color="Yellow (595nm)" current=0.030 package="5 mm [THT]"]
  LED3 = LED - 5mm [color="Green (560nm)" current=0.030 package="5 mm [THT]"]
  R1 = Resistor [tolerance=±5% power=0.25 resistance=220 package=THT]
  R2 = Resistor [tolerance=±5% power=0.25 resistance=220 package=THT]
  R3 = Resistor [tolerance=±5% power=0.25 resistance=220 package=THT]
  BT1 = Bluetooth HC-06u [package=THT]
  Teensy_LC1 = Teensy-LC

nets:
  N1: LED1.cathode, R1.Pin_1
  N2: LED1.anode, Teensy_LC1.D2
  N3: LED2.cathode, R2.Pin_1
  N4: LED2.anode, Teensy_LC1.D3
  N5: LED3.cathode, R3.Pin_1
  N6: LED3.anode, Teensy_LC1.D4
  GND: R1.Pin_0, R2.Pin_0, R3.Pin_0, BT1.GND, Teensy_LC1.GND
  VCC: BT1.VCC, Teensy_LC1.Vin
  N7: BT1.TXD, Teensy_LC1.D0
  N8: BT1.RXD, Teensy_LC1.D1
  N9: Teensy_LC1.D12, Teensy_LC1.5Vout
  N10: Teensy_LC1.Program, Teensy_LC1.A12/DAC, Teensy_LC1.D13
  N11: Teensy_LC1.A7/D21, Teensy_LC1.A11
  N12: Teensy_LC1.A8/D22, Teensy_LC1.A10
  N13: Teensy_LC1.A9/D23, Teensy_LC1.AREF
  N14: Teensy_LC1.AGND, Teensy_LC1.VUSB

custom parts:
  Bluetooth HC-06u: Bluetooth HC-06 - face up, pins down 16.5mm x 37.5mm PCB
  Teensy-LC: Teensy-LC (Low Cost) is a powerful 32 bit microcontroller board, with a rich set of hardware peripherals, at a very affordable price! Teensy-LC delivers an impressive collection of capabilities to make modern electronic projects simpler. It features an ARM Cortex-M0+ processor at 48 MHz, 62K Flash, 8K RAM, 12 bit analog input & output, hardware Serial, SPI & I2C, USB, and a total of 27 I/O pins.
